# Fritzing sketch gasDetector (saved by Fritzing 0.9.9b)

parts:
  Digispark1 = Digispark
  BAT1 = Battery Holders [package=battery-aa]
  BAT2 = Battery Holders [package=battery-aa]
  BAT3 = Battery Holders [package=battery-aa]
  BAT4 = Battery Holders [package=battery-aa]
  SG1 = Buzzer 12mm [package=buzzer-12mm-ns]
  LED1 = smd LED [color="Red (633nm)" package="0603 [SMD]"]
  R1 = Resistor [tolerance=±5% resistance=2.2k package="0603 [SMD]"]
  R2 = Resistor [tolerance=±5% resistance=220 package="0603 [SMD]"]
  MQ-4 = MQ-4
  U1 = SWITCH-SPST-2 [package=switch-spst-vertical]
  Q1 = NPN-Transistor [package="TO92 [THT]"]

nets:
  VCC: Digispark1.VCC, SG1.1, MQ-4.VCC
  GND: Digispark1.GND, BAT1.-, LED1.cathode, MQ-4.GND, Q1.E
  N1: Digispark1.VIN, U1.P
  N2: Digispark1.P0, R2.Pin_0
  N3: Digispark1.P1, R1.Pin_0
  N4: Digispark1.P2, MQ-4.AO
  N5: BAT1.+, BAT2.-
  N6: BAT2.+, BAT3.-
  N7: BAT3.+, BAT4.-
  N8: BAT4.+, U1.O
  N9: SG1.2, Q1.C
  N10: LED1.anode, R2.Pin_1
  N11: R1.Pin_1, Q1.B

custom parts:
  Digispark: The Digispark is an Attiny85 based microcontroller development board similar to the Arduino line, only cheaper, smaller, and a bit less powerful. With a whole host of shields to extend its functionality and the ability to use the familiar Arduino IDE the Digispark is a great way to jump into electronics, or perfect for when an Arduino is too big or too much.
